// Logisim project controller.circ as structural Verilog
module Y (
  input  [31:0] in_1,
  input  reset_pos,
  input  in_3
);

  wire clock_1_out, not_1_out, t_ff_1_q;
  wire [4:0] undriven;
  wire [31:0] controlled_buffer_1_out, multiplexer_1_out, shifter_1_out, shifter_2_out;

  T_Flip_Flop t_ff_1 (.clk(in_3), .T(1'b1), .Q(t_ff_1_q));  // open: Qn, preset, reset, en
  Shifter #(.width(32)) shifter_1 (.in(in_1), .\dist (undriven), .out(shifter_1_out));
  Shifter #(.width(32), .shift("lr")) shifter_2 (.in(in_1), .\dist (undriven), .out(shifter_2_out));
  Multiplexer #(.width(32), .enable("false")) multiplexer_1 (
    .in0(shifter_1_out), .in1(shifter_2_out), .out(multiplexer_1_out), .sel(t_ff_1_q));
  assign controlled_buffer_1_out = not_1_out ? multiplexer_1_out : 32'bz;  // Controlled_Buffer controlled_buffer_1
  not not_1 (not_1_out, reset_pos);
  assign controlled_buffer_1_out = reset_pos ? 32'h4 : 32'bz;  // Controlled_Buffer controlled_buffer_2
  Register #(.width(32)) register_1 (.D(controlled_buffer_1_out), .Q(in_1), .clr(clock_1_out));  // open: en, clk
  Clock clock_1 (.out(clock_1_out));

  // Notes on the sheet:
  //   Движение по VY
endmodule

module X (
  input  [31:0] in_1,
  input  reset_pos,
  input  in_3
);

  wire clock_1_out, not_1_out, t_ff_1_q;
  wire [4:0] undriven;
  wire [31:0] controlled_buffer_1_out, multiplexer_1_out, shifter_1_out, shifter_2_out;

  Shifter #(.width(32)) shifter_1 (.in(in_1), .\dist (undriven), .out(shifter_1_out));
  Shifter #(.width(32), .shift("lr")) shifter_2 (.in(in_1), .\dist (undriven), .out(shifter_2_out));
  T_Flip_Flop t_ff_1 (.clk(in_3), .T(1'b1), .Q(t_ff_1_q));  // open: Qn, preset, reset, en
  Multiplexer #(.width(32), .enable("false")) multiplexer_1 (
    .in0(shifter_1_out), .in1(shifter_2_out), .out(multiplexer_1_out), .sel(t_ff_1_q));
  assign controlled_buffer_1_out = not_1_out ? multiplexer_1_out : 32'bz;  // Controlled_Buffer controlled_buffer_1
  not not_1 (not_1_out, reset_pos);
  assign controlled_buffer_1_out = reset_pos ? 32'h4 : 32'bz;  // Controlled_Buffer controlled_buffer_2
  Clock clock_1 (.out(clock_1_out));
  Register #(.width(32)) register_1 (.D(controlled_buffer_1_out), .Q(in_1), .clr(clock_1_out));  // open: en, clk

  // Notes on the sheet:
  //   Движение по VX
endmodule

module XX (
  input  [31:0] in_1,
  input  reset_pos,
  input  Go_Up,
  input  Go_Down
);

  wire clock_1_out, not_1_out;
  wire [4:0] undriven;
  wire [31:0] controlled_buffer_1_out, multiplexer_1_out, shifter_1_out, shifter_2_out;

  Shifter #(.width(32)) shifter_1 (.in(in_1), .\dist (undriven), .out(shifter_1_out));
  Shifter #(.width(32), .shift("lr")) shifter_2 (.in(in_1), .\dist (undriven), .out(shifter_2_out));
  Multiplexer #(.select(2), .width(32), .enable("false")) multiplexer_1 (
    .in0(in_1), .in1(shifter_1_out), .in3(shifter_2_out), .out(multiplexer_1_out), .sel({Go_Down, Go_Up}));  // open: in2
  assign controlled_buffer_1_out = not_1_out ? multiplexer_1_out : 32'bz;  // Controlled_Buffer controlled_buffer_1
  not not_1 (not_1_out, reset_pos);
  assign controlled_buffer_1_out = reset_pos ? 32'h4 : 32'bz;  // Controlled_Buffer controlled_buffer_2
  Register #(.width(32)) register_1 (.D(controlled_buffer_1_out), .Q(in_1), .clr(clock_1_out));  // open: en, clk
  Clock clock_1 (.out(clock_1_out));
endmodule

module YY (
  input  [31:0] in_1,
  input  reset_pos,
  input  Go_Up,
  input  Go_Down
);

  wire clock_1_out, not_1_out;
  wire [4:0] undriven;
  wire [31:0] controlled_buffer_1_out, multiplexer_1_out, shifter_1_out, shifter_2_out;

  Shifter #(.width(32)) shifter_1 (.in(in_1), .\dist (undriven), .out(shifter_1_out));
  Shifter #(.width(32), .shift("lr")) shifter_2 (.in(in_1), .\dist (undriven), .out(shifter_2_out));
  Multiplexer #(.select(2), .width(32), .enable("false")) multiplexer_1 (
    .in0(in_1), .in1(shifter_1_out), .in3(shifter_2_out), .out(multiplexer_1_out), .sel({Go_Down, Go_Up}));  // open: in2
  assign controlled_buffer_1_out = not_1_out ? multiplexer_1_out : 32'bz;  // Controlled_Buffer controlled_buffer_1
  not not_1 (not_1_out, reset_pos);
  assign controlled_buffer_1_out = reset_pos ? 32'h4 : 32'bz;  // Controlled_Buffer controlled_buffer_2
  Register #(.width(32)) register_1 (.D(controlled_buffer_1_out), .Q(in_1), .clr(clock_1_out));  // open: en, clk
  Clock clock_1 (.out(clock_1_out));
endmodule

module Hit (
  input  [31:0] in_1,
  input  [31:0] in_2,
  input  in_3
);

  wire and_2_out, or_1_out;
  wire [31:0] and_1_out;

  assign and_1_out = in_1 & in_2;  // AND_Gate and_1, 32 bits wide
  or or_1 (or_1_out, and_1_out[0], and_1_out[1], and_1_out[2], and_1_out[3], and_1_out[4], and_1_out[5], and_1_out[6], and_1_out[7], and_1_out[8], and_1_out[9], and_1_out[10], and_1_out[11], and_1_out[12], and_1_out[13], and_1_out[14], and_1_out[15], and_1_out[16], and_1_out[17], and_1_out[18], and_1_out[19], and_1_out[20], and_1_out[21], and_1_out[22], and_1_out[23], and_1_out[24], and_1_out[25], and_1_out[26], and_1_out[27], and_1_out[28], and_1_out[29], and_1_out[30], and_1_out[31]);
  and and_2 (and_2_out, or_1_out, in_3);
  // Probe on and_2_out
endmodule
