// Logisim project sravnenie.circ as structural Verilog: 3 circuits, main circuit sravnitel 5 bitov
module sravnitel_5_bitov (
  input  [4:0] in_1,
  input  [4:0] in_2,
  output out_3
);

  wire [4:0] xor_1_out;

  assign xor_1_out = in_1 ^ in_2;  // XOR_Gate xor_1, 5 bits wide
  nor nor_1 (out_3, xor_1_out[0], xor_1_out[1], xor_1_out[2], xor_1_out[3], xor_1_out[4]);
endmodule

module \Двигалка_битов  (
  input  [4:0] \input ,
  output [31:0] \output 
);

  Shifter #(.width(32)) shifter_1 (.in(32'h1), .\dist (\input ), .out(\output ));
endmodule

module _1_VAl_0_0 (
  input  [4:0] in_1,
  input  in_2,
  output [4:0] out_3
);

  wire not_1_out;

  assign out_3 = in_2 ? in_1 : 5'bz;  // Controlled_Buffer controlled_buffer_1
  assign out_3 = not_1_out ? {5{1'b0}} : 5'bz;  // Controlled_Buffer controlled_buffer_2
  not not_1 (not_1_out, in_2);
endmodule
