// Logisim project test__kopia.circ as structural Verilog: 1 circuit, main circuit main
module main (
  input  [4:0] in_1
);

  wire [4:0] joystick_1_x, joystick_1_y, joystick_2_y, joystick_3_y, videosector_1_ballx_2,
       videosector_1_bally_2, videosector_1_chipid_2, videosector_1_leftbat_2, videosector_1_rightbat_2,
       videosector_2_ballx_2, videosector_2_bally_2, videosector_2_chipid_2, videosector_2_leftbat_2,
       videosector_2_rightbat_2, videosector_3_ballx_2, videosector_3_bally_2, videosector_3_chipid_2,
       videosector_3_leftbat_2, videosector_3_rightbat_2;
  wire [31:0] videosector_1_out_6, videosector_1_out_7, videosector_1_out_8, videosector_1_out_9,
       videosector_1_out_10, videosector_1_out_11, videosector_1_out_12, videosector_1_out_13,
       videosector_2_out_6, videosector_2_out_7, videosector_2_out_8, videosector_2_out_9,
       videosector_2_out_10, videosector_2_out_11, videosector_2_out_12, videosector_2_out_13,
       videosector_3_out_6, videosector_3_out_7, videosector_3_out_8, videosector_3_out_9,
       videosector_3_out_10, videosector_3_out_11, videosector_3_out_12, videosector_3_out_13,
       videosector_4_out_6, videosector_4_out_7, videosector_4_out_8, videosector_4_out_9,
       videosector_4_out_10, videosector_4_out_11, videosector_4_out_12, videosector_4_out_13;

  Joystick #(.bits(5)) joystick_1 (.x(joystick_1_x), .y(joystick_1_y));
  Joystick #(.bits(5)) joystick_2 (.y(joystick_2_y));  // open: x
  Joystick #(.bits(5)) joystick_3 (.y(joystick_3_y));  // open: x
  DotMatrix #(.matrixcols(32), .matrixrows(32)) dotmatrix_1 (
    .col0(videosector_1_out_6), .col1(videosector_1_out_7), .col2(videosector_1_out_8),
    .col3(videosector_1_out_9), .col4(videosector_1_out_10), .col5(videosector_1_out_11),
    .col6(videosector_1_out_12), .col7(videosector_1_out_13), .col8(videosector_2_out_6),
    .col9(videosector_2_out_7), .col10(videosector_2_out_8), .col11(videosector_2_out_9),
    .col12(videosector_2_out_10), .col13(videosector_2_out_11), .col14(videosector_2_out_12),
    .col15(videosector_2_out_13), .col16(videosector_3_out_6), .col17(videosector_3_out_7),
    .col18(videosector_3_out_8), .col19(videosector_3_out_9), .col20(videosector_3_out_10),
    .col21(videosector_3_out_11), .col22(videosector_3_out_12), .col23(videosector_3_out_13),
    .col24(videosector_4_out_6), .col25(videosector_4_out_7), .col26(videosector_4_out_8),
    .col27(videosector_4_out_9), .col28(videosector_4_out_10), .col29(videosector_4_out_11),
    .col30(videosector_4_out_12), .col31(videosector_4_out_13));
  VideoSector videosector_1 (
    .BallY(joystick_1_x), .BallX(joystick_1_y), .LeftBat(joystick_2_y), .rightBat(joystick_3_y),
    .ChipId(in_1), .BallY_2(videosector_1_bally_2), .BallX_2(videosector_1_ballx_2),
    .LeftBat_2(videosector_1_leftbat_2), .rightBat_2(videosector_1_rightbat_2),
    .ChipId_2(videosector_1_chipid_2), .out_6(videosector_1_out_6), .out_7(videosector_1_out_7),
    .out_8(videosector_1_out_8), .out_9(videosector_1_out_9), .out_10(videosector_1_out_10),
    .out_11(videosector_1_out_11), .out_12(videosector_1_out_12), .out_13(videosector_1_out_13));
  VideoSector videosector_2 (
    .BallY(videosector_1_bally_2), .BallX(videosector_1_ballx_2), .LeftBat(videosector_1_leftbat_2),
    .rightBat(videosector_1_rightbat_2), .ChipId(videosector_1_chipid_2), .BallY_2(videosector_2_bally_2),
    .BallX_2(videosector_2_ballx_2), .LeftBat_2(videosector_2_leftbat_2),
    .rightBat_2(videosector_2_rightbat_2), .ChipId_2(videosector_2_chipid_2), .out_6(videosector_2_out_6),
    .out_7(videosector_2_out_7), .out_8(videosector_2_out_8), .out_9(videosector_2_out_9),
    .out_10(videosector_2_out_10), .out_11(videosector_2_out_11), .out_12(videosector_2_out_12),
    .out_13(videosector_2_out_13));
  VideoSector videosector_3 (
    .BallY(videosector_2_bally_2), .BallX(videosector_2_ballx_2), .LeftBat(videosector_2_leftbat_2),
    .rightBat(videosector_2_rightbat_2), .ChipId(videosector_2_chipid_2), .BallY_2(videosector_3_bally_2),
    .BallX_2(videosector_3_ballx_2), .LeftBat_2(videosector_3_leftbat_2),
    .rightBat_2(videosector_3_rightbat_2), .ChipId_2(videosector_3_chipid_2), .out_6(videosector_3_out_6),
    .out_7(videosector_3_out_7), .out_8(videosector_3_out_8), .out_9(videosector_3_out_9),
    .out_10(videosector_3_out_10), .out_11(videosector_3_out_11), .out_12(videosector_3_out_12),
    .out_13(videosector_3_out_13));
  VideoSector videosector_4 (
    .BallY(videosector_3_bally_2), .BallX(videosector_3_ballx_2), .LeftBat(videosector_3_leftbat_2),
    .rightBat(videosector_3_rightbat_2), .ChipId(videosector_3_chipid_2), .out_6(videosector_4_out_6),
    .out_7(videosector_4_out_7), .out_8(videosector_4_out_8), .out_9(videosector_4_out_9),
    .out_10(videosector_4_out_10), .out_11(videosector_4_out_11), .out_12(videosector_4_out_12),
    .out_13(videosector_4_out_13));  // open: BallY_2, BallX_2, LeftBat_2, rightBat_2, ChipId_2
endmodule
