// Logisim project videoChip.circ as structural Verilog: 1 circuit, main circuit videoChip
module videoChip (
  input  [4:0] bally,
  input  [4:0] ballx,
  input  [4:0] leftBatY,
  input  [4:0] rightBatY,
  input  [4:0] ChipID,
  output [4:0] ballY_2,
  output [4:0] leftBat,
  output [4:0] rightBat,
  output [4:0] ballY_3,
  output [4:0] ballx_2,
  output [4:0] leftBatY_2,
  output [4:0] rightBatY_2,
  output [4:0] ChipID_2
);

  wire sravnitel_5_bitov_1_out_3, sravnitel_5_bitov_2_out_3, sravnitel_5_bitov_3_out_3;

  sravnitel_5_bitov sravnitel_5_bitov_1 (.in_1(5'b00011), .in_2(ChipID), .out_3(sravnitel_5_bitov_1_out_3));
  _1_VAl_0_0 u_1_val_0_0_1 (.in_1(rightBatY), .in_2(sravnitel_5_bitov_1_out_3), .out_3(rightBat));
  sravnitel_5_bitov sravnitel_5_bitov_2 (.in_1(5'b11100), .in_2(ChipID), .out_3(sravnitel_5_bitov_2_out_3));
  _1_VAl_0_0 u_1_val_0_0_2 (.in_1(leftBatY), .in_2(sravnitel_5_bitov_2_out_3), .out_3(leftBat));
  Adder #(.width(5)) adder_1 (.a(ChipID), .b(5'b00001), .out(ChipID_2));  // open: cin, cout
  _1_VAl_0_0 u_1_val_0_0_3 (.in_1(bally), .in_2(sravnitel_5_bitov_3_out_3), .out_3(ballY_2));
  sravnitel_5_bitov sravnitel_5_bitov_3 (.in_1(ballx), .in_2(ChipID), .out_3(sravnitel_5_bitov_3_out_3));

  assign ballx_2 = ballx;
  assign ballY_3 = bally;
  assign leftBatY_2 = leftBatY;
  assign rightBatY_2 = rightBatY;

  // Other names for the same wires on the sheet: _1[4:0] = bally; _2[4:0] = ballx; _3[4:0] = leftBatY;
  //   _4[4:0] = rightBatY
endmodule
