// Logisim project videoSector.circ as structural Verilog: 4 circuits, main circuit levelUpedVideoChip
module levelUpedVideoChip (
  input  [4:0] ballY,
  input  [4:0] ballX,
  input  [4:0] laftBat,
  input  [4:0] rightBat,
  input  [4:0] chipID,
  output [31:0] out_6,
  output [4:0] ballY_2,
  output [4:0] ballX_2,
  output [4:0] laftBat_2,
  output [4:0] rightBat_2,
  output [4:0] chipID_2
);

  wire videochepv1_1_ball__0, videochepv1_1_lbat__0, videochepv1_1_rbat__0;
  wire [4:0] videochepv1_1_bally_2, videochepv1_1_leftbat, videochepv1_1_rightbat;
  wire [31:0] multiplexer_1_out, multiplexer_2_out, multiplexer_3_out, \двигалка_битов_1_output ,
       \двигалка_битов_2_output , \двигалка_битов_3_output , \добавлялкасоседейдляракеток_1_out_2 ,
       \добавлялкасоседейдляракеток_2_out_2 ;

  Multiplexer #(.width(32)) multiplexer_1 (
    .in0({32{1'b0}}), .in1(\двигалка_битов_1_output ), .out(multiplexer_1_out), .sel(videochepv1_1_ball__0));  // open: en
  \Двигалка_битов  \u_двигалка_битов_1  (.\input (videochepv1_1_bally_2), .\output (\двигалка_битов_1_output ));
  videoChepV1 videochepv1_1 (
    .bally(ballY), .ballx(ballX), .leftBatY(laftBat), .rightBatY(rightBat), .ChipID(chipID),
    .Ball__0(videochepv1_1_ball__0), .RBat__0(videochepv1_1_rbat__0), .lBat__0(videochepv1_1_lbat__0),
    .ballY_2(videochepv1_1_bally_2), .leftBat(videochepv1_1_leftbat), .rightBat(videochepv1_1_rightbat),
    .ballY_3(ballY_2), .ballx_2(ballX_2), .leftBatY_2(laftBat_2), .rightBatY_2(rightBat_2),
    .ChipID_2(chipID_2));
  assign out_6 = multiplexer_1_out | multiplexer_2_out | multiplexer_3_out;  // OR_Gate or_1, 32 bits wide
  Multiplexer #(.width(32)) multiplexer_2 (
    .in0({32{1'b0}}), .in1(\добавлялкасоседейдляракеток_1_out_2 ), .out(multiplexer_2_out),
    .sel(videochepv1_1_lbat__0));  // open: en
  \добавлялкаСоседейдляРакеток  \u_добавлялкасоседейдляракеток_1  (
    .in_1(\двигалка_битов_2_output ), .out_2(\добавлялкасоседейдляракеток_1_out_2 ));
  \Двигалка_битов  \u_двигалка_битов_2  (.\input (videochepv1_1_leftbat), .\output (\двигалка_битов_2_output ));
  Multiplexer #(.width(32)) multiplexer_3 (
    .in0({32{1'b0}}), .in1(\добавлялкасоседейдляракеток_2_out_2 ), .out(multiplexer_3_out),
    .sel(videochepv1_1_rbat__0));  // open: en
  \добавлялкаСоседейдляРакеток  \u_добавлялкасоседейдляракеток_2  (
    .in_1(\двигалка_битов_3_output ), .out_2(\добавлялкасоседейдляракеток_2_out_2 ));
  \Двигалка_битов  \u_двигалка_битов_3  (.\input (videochepv1_1_rightbat), .\output (\двигалка_битов_3_output ));
endmodule

module VideoSector (
  input  [4:0] BallY,
  input  [4:0] BallX,
  input  [4:0] LeftBat,
  input  [4:0] rightBat,
  input  [4:0] ChipId,
  output [31:0] out_6,
  output [31:0] out_7,
  output [31:0] out_8,
  output [31:0] out_9,
  output [31:0] out_10,
  output [31:0] out_11,
  output [31:0] out_12,
  output [31:0] out_13,
  output [4:0] BallY_2,
  output [4:0] BallX_2,
  output [4:0] LeftBat_2,
  output [4:0] rightBat_2,
  output [4:0] ChipId_2
);

  wire [4:0] levelupedvideochip_1_ballx_2, levelupedvideochip_1_bally_2, levelupedvideochip_1_chipid_2,
       levelupedvideochip_1_laftbat_2, levelupedvideochip_1_rightbat_2, levelupedvideochip_2_ballx_2,
       levelupedvideochip_2_bally_2, levelupedvideochip_2_chipid_2, levelupedvideochip_2_laftbat_2,
       levelupedvideochip_2_rightbat_2, levelupedvideochip_3_ballx_2, levelupedvideochip_3_bally_2,
       levelupedvideochip_3_chipid_2, levelupedvideochip_3_laftbat_2, levelupedvideochip_3_rightbat_2,
       levelupedvideochip_4_ballx_2, levelupedvideochip_4_bally_2, levelupedvideochip_4_chipid_2,
       levelupedvideochip_4_laftbat_2, levelupedvideochip_4_rightbat_2, levelupedvideochip_5_ballx_2,
       levelupedvideochip_5_bally_2, levelupedvideochip_5_chipid_2, levelupedvideochip_5_laftbat_2,
       levelupedvideochip_5_rightbat_2, levelupedvideochip_6_ballx_2, levelupedvideochip_6_bally_2,
       levelupedvideochip_6_chipid_2, levelupedvideochip_6_laftbat_2, levelupedvideochip_6_rightbat_2,
       levelupedvideochip_7_ballx_2, levelupedvideochip_7_bally_2, levelupedvideochip_7_chipid_2,
       levelupedvideochip_7_laftbat_2, levelupedvideochip_7_rightbat_2;

  levelUpedVideoChip levelupedvideochip_1 (
    .ballY(BallY), .ballX(BallX), .laftBat(LeftBat), .rightBat(rightBat), .chipID(ChipId), .out_6(out_6),
    .ballY_2(levelupedvideochip_1_bally_2), .ballX_2(levelupedvideochip_1_ballx_2),
    .laftBat_2(levelupedvideochip_1_laftbat_2), .rightBat_2(levelupedvideochip_1_rightbat_2),
    .chipID_2(levelupedvideochip_1_chipid_2));
  levelUpedVideoChip levelupedvideochip_2 (
    .ballY(levelupedvideochip_1_bally_2), .ballX(levelupedvideochip_1_ballx_2),
    .laftBat(levelupedvideochip_1_laftbat_2), .rightBat(levelupedvideochip_1_rightbat_2),
    .chipID(levelupedvideochip_1_chipid_2), .out_6(out_7), .ballY_2(levelupedvideochip_2_bally_2),
    .ballX_2(levelupedvideochip_2_ballx_2), .laftBat_2(levelupedvideochip_2_laftbat_2),
    .rightBat_2(levelupedvideochip_2_rightbat_2), .chipID_2(levelupedvideochip_2_chipid_2));
  levelUpedVideoChip levelupedvideochip_3 (
    .ballY(levelupedvideochip_5_bally_2), .ballX(levelupedvideochip_5_ballx_2),
    .laftBat(levelupedvideochip_5_laftbat_2), .rightBat(levelupedvideochip_5_rightbat_2),
    .chipID(levelupedvideochip_5_chipid_2), .out_6(out_10), .ballY_2(levelupedvideochip_3_bally_2),
    .ballX_2(levelupedvideochip_3_ballx_2), .laftBat_2(levelupedvideochip_3_laftbat_2),
    .rightBat_2(levelupedvideochip_3_rightbat_2), .chipID_2(levelupedvideochip_3_chipid_2));
  levelUpedVideoChip levelupedvideochip_4 (
    .ballY(levelupedvideochip_2_bally_2), .ballX(levelupedvideochip_2_ballx_2),
    .laftBat(levelupedvideochip_2_laftbat_2), .rightBat(levelupedvideochip_2_rightbat_2),
    .chipID(levelupedvideochip_2_chipid_2), .out_6(out_8), .ballY_2(levelupedvideochip_4_bally_2),
    .ballX_2(levelupedvideochip_4_ballx_2), .laftBat_2(levelupedvideochip_4_laftbat_2),
    .rightBat_2(levelupedvideochip_4_rightbat_2), .chipID_2(levelupedvideochip_4_chipid_2));
  levelUpedVideoChip levelupedvideochip_5 (
    .ballY(levelupedvideochip_4_bally_2), .ballX(levelupedvideochip_4_ballx_2),
    .laftBat(levelupedvideochip_4_laftbat_2), .rightBat(levelupedvideochip_4_rightbat_2),
    .chipID(levelupedvideochip_4_chipid_2), .out_6(out_9), .ballY_2(levelupedvideochip_5_bally_2),
    .ballX_2(levelupedvideochip_5_ballx_2), .laftBat_2(levelupedvideochip_5_laftbat_2),
    .rightBat_2(levelupedvideochip_5_rightbat_2), .chipID_2(levelupedvideochip_5_chipid_2));
  levelUpedVideoChip levelupedvideochip_6 (
    .ballY(levelupedvideochip_7_bally_2), .ballX(levelupedvideochip_7_ballx_2),
    .laftBat(levelupedvideochip_7_laftbat_2), .rightBat(levelupedvideochip_7_rightbat_2),
    .chipID(levelupedvideochip_7_chipid_2), .out_6(out_12), .ballY_2(levelupedvideochip_6_bally_2),
    .ballX_2(levelupedvideochip_6_ballx_2), .laftBat_2(levelupedvideochip_6_laftbat_2),
    .rightBat_2(levelupedvideochip_6_rightbat_2), .chipID_2(levelupedvideochip_6_chipid_2));
  levelUpedVideoChip levelupedvideochip_7 (
    .ballY(levelupedvideochip_3_bally_2), .ballX(levelupedvideochip_3_ballx_2),
    .laftBat(levelupedvideochip_3_laftbat_2), .rightBat(levelupedvideochip_3_rightbat_2),
    .chipID(levelupedvideochip_3_chipid_2), .out_6(out_11), .ballY_2(levelupedvideochip_7_bally_2),
    .ballX_2(levelupedvideochip_7_ballx_2), .laftBat_2(levelupedvideochip_7_laftbat_2),
    .rightBat_2(levelupedvideochip_7_rightbat_2), .chipID_2(levelupedvideochip_7_chipid_2));
  levelUpedVideoChip levelupedvideochip_8 (
    .ballY(levelupedvideochip_6_bally_2), .ballX(levelupedvideochip_6_ballx_2),
    .laftBat(levelupedvideochip_6_laftbat_2), .rightBat(levelupedvideochip_6_rightbat_2),
    .chipID(levelupedvideochip_6_chipid_2), .out_6(out_13), .ballY_2(BallY_2), .ballX_2(BallX_2),
    .laftBat_2(LeftBat_2), .rightBat_2(rightBat_2), .chipID_2(ChipId_2));
endmodule

module videoChepV1 (
  input  [4:0] bally,
  input  [4:0] ballx,
  input  [4:0] leftBatY,
  input  [4:0] rightBatY,
  input  [4:0] ChipID,
  output Ball__0,
  output RBat__0,
  output lBat__0,
  output [4:0] ballY_2,
  output [4:0] leftBat,
  output [4:0] rightBat,
  output [4:0] ballY_3,
  output [4:0] ballx_2,
  output [4:0] leftBatY_2,
  output [4:0] rightBatY_2,
  output [4:0] ChipID_2
);

  sravnitel_5_bitov sravnitel_5_bitov_1 (.in_1(5'b00011), .in_2(ChipID), .out_3(RBat__0));
  assign rightBat = RBat__0 ? rightBatY : 5'bz;  // Controlled_Buffer controlled_buffer_1
  sravnitel_5_bitov sravnitel_5_bitov_2 (.in_1(5'b11100), .in_2(ChipID), .out_3(lBat__0));
  assign leftBat = lBat__0 ? leftBatY : 5'bz;  // Controlled_Buffer controlled_buffer_2
  Adder #(.width(5)) adder_1 (.a(ChipID), .b(5'b00001), .out(ChipID_2));  // open: cin, cout
  assign ballY_2 = Ball__0 ? bally : 5'bz;  // Controlled_Buffer controlled_buffer_3
  sravnitel_5_bitov sravnitel_5_bitov_3 (.in_1(ballx), .in_2(ChipID), .out_3(Ball__0));

  assign ballx_2 = ballx;
  assign ballY_3 = bally;
  assign leftBatY_2 = leftBatY;
  assign rightBatY_2 = rightBatY;

  // Other names for the same wires on the sheet: _1[4:0] = bally; _2[4:0] = ballx; _3[4:0] = leftBatY;
  //   _4[4:0] = rightBatY
endmodule

module \добавлялкаСоседейдляРакеток  (
  input  [31:0] in_1,
  output [31:0] out_2
);

  wire [31:0] adder_1_out, shifter_1_out, shifter_2_out;

  Shifter #(.width(32)) shifter_1 (.in(in_1), .\dist (5'b00001), .out(shifter_1_out));
  Shifter #(.width(32), .shift("lr")) shifter_2 (.in(in_1), .\dist (5'b00001), .out(shifter_2_out));
  Adder #(.width(32)) adder_1 (.a(in_1), .b(shifter_1_out), .out(adder_1_out));  // open: cin, cout
  Adder #(.width(32)) adder_2 (.a(adder_1_out), .b(shifter_2_out), .out(out_2));  // open: cin, cout
endmodule
